# Fritzing sketch board (saved by Fritzing 0.9.3b)
circuit board: 6.3cm x 3.9cm
breadboards: 1

parts:
  RST = Pushbutton [package="[THT]"]
  R_SYNC = Resistor [tolerance=±5% resistance=220 package=THT]
  R_CLR = Resistor [tolerance=±5% resistance=220 package=THT]
  WeMos_D1_Mini1 = WeMos D1 Mini
  CLR = LED - 3mm [color="White (6500K)" package="3 mm [THT]"]
  SYNC = LED - 3mm [color="White (6500K)" package="3 mm [THT]"]
  H_LUX = male pin header, 2 pins [form="♂ (male)"]
  LUX = PHOTOCELL [package=photocell]
  R_LUX = Resistor [tolerance=±5% resistance=10k package=THT]
  JP1 = Header 2 [package=jst-2-pth]
  OLED = Grove OLED 128x96

nets:
  N1: RST.Pin_1, RST.Pin_2, WeMos_D1_Mini1.D8
  N2: RST.Pin_3, RST.Pin_4, WeMos_D1_Mini1.G, CLR.cathode, SYNC.cathode, R_LUX.Pin_1, OLED.GND
  N3: R_SYNC.Pin_0, SYNC.anode
  N4: R_SYNC.Pin_1, WeMos_D1_Mini1.D3
  N5: R_CLR.Pin_0, CLR.anode
  N6: R_CLR.Pin_1, WeMos_D1_Mini1.D5
  5V: WeMos_D1_Mini1.5V, H_LUX.pin1, LUX.P$1, JP1.2, OLED.VCC
  N7: WeMos_D1_Mini1.A0, H_LUX.pin2, LUX.P$2, R_LUX.Pin_0, JP1.1
  N8: WeMos_D1_Mini1.D1, OLED.SCL
  N9: WeMos_D1_Mini1.D2, OLED.SDA
